# Fritzing sketch Boiler sensor schematic (saved by Fritzing 0.9.2b)
breadboards: 1

parts:
  Part1 = Arduino Nano (Rev3.0)
  R1 = Temperature Sensor (Thermistor) [thermistor_type=NTC package=THT]
  R2 = Resistor [tolerance=±5% resistance=220 package="1206 [SMD]"]
  U3 = Mystery Part - 3 pins [chip_label=? package=THT]

nets:
  GND: Part1.GND, R2.Pin_1, U3.GND
  5V: Part1.5V, R1.pin_1, U3.Vin
  N1: Part1.A5, U3.Vout
  N2: Part1.A0, R1.pin_0, R2.Pin_0

notes:
  Modern Device Current Sensor

custom parts:
  Mystery Part - 3 pins: A dummy, proxy, ersatz, stand-in part for whatever you want. With 3 pins on a 100 mil inline pin header footprint.
